# Fritzing sketch Four_Light_Panel (saved by Fritzing 0.8.0b)
breadboards: 1

parts:
  Part1 = Arduino Uno (Rev3)
  LED4 = LED - 5mm [color="Red (633nm)" package="5 mm [THT]"]
  LED5 = LED - 5mm [color="Blue (525nm)" package="5 mm [THT]"]
  LED6 = LED - 5mm [color="Yellow (595nm)" package="5 mm [THT]"]
  LED7 = LED - 5mm [color="Green (565nm)" package="5 mm [THT]"]
  R1 = Resistor [tolerance=±5% resistance=220 package=THT]
  R2 = Resistor [tolerance=±5% resistance=220 package=THT]
  R3 = Resistor [tolerance=±5% resistance=220 package=THT]
  R4 = Resistor [tolerance=±5% resistance=220 package=THT]
  S1 = Pushbutton [package=THT]
  S2 = Pushbutton [package=THT]
  S3 = Pushbutton [package=THT]
  S4 = Pushbutton [package=THT]
  R5 = Resistor [tolerance=±5% resistance=10k package=THT]
  R6 = Resistor [tolerance=±5% resistance=10k package=THT]
  R7 = Resistor [tolerance=±5% resistance=10k package=THT]
  R8 = Resistor [tolerance=±5% resistance=10k package=THT]

nets:
  N1: Part1.GND, R1.Pin_1, R2.Pin_1, R3.Pin_1, R4.Pin_1, R5.Pin_1, R6.Pin_1, R7.Pin_1, R8.Pin_1
  N2: Part1.D8, LED6.anode
  N3: Part1.D9_PWM, LED5.anode
  N4: Part1.D2, S2.leg1, R5.Pin_0
  N5: Part1.D3_PWM, S3.leg1, R6.Pin_0
  N6: Part1.D4, S4.leg1, R7.Pin_0
  N7: Part1.D5_PWM, S1.leg1, R8.Pin_0
  N8: Part1.D6_PWM, LED7.anode
  N9: Part1.D7, LED4.anode
  N10: Part1.5V, S1.leg0, S2.leg0, S3.leg0, S4.leg0
  N11: LED4.cathode, R3.Pin_0
  N12: LED5.cathode, R1.Pin_0
  N13: LED6.cathode, R2.Pin_0
  N14: LED7.cathode, R4.Pin_0
