# Fritzing sketch Four_Light_Panel_No_Code (saved by Fritzing 0.8.0b)
breadboards: 1

parts:
  Part1 = Arduino Uno (Rev3)
  S1 = Pushbutton [package=THT]
  S2 = Pushbutton [package=THT]
  S3 = Pushbutton [package=THT]
  S4 = Pushbutton [package=THT]
  LED1 = LED - 5mm [color="Green (565nm)" package="5 mm [THT]"]
  LED2 = LED - 5mm [color="Red (633nm)" package="5 mm [THT]"]
  LED3 = LED - 5mm [color="Yellow (595nm)" package="5 mm [THT]"]
  LED4 = LED - 5mm [color="Blue (505nm)" package="5 mm [THT]"]
  R1 = Resistor [tolerance=±5% resistance=220 package=THT]
  R2 = Resistor [tolerance=±5% resistance=220 package=THT]
  R3 = Resistor [tolerance=±5% resistance=220 package=THT]
  R4 = Resistor [tolerance=±5% resistance=220 package=THT]

nets:
  N1: Part1.GND, LED1.cathode, LED2.cathode, LED3.cathode, LED4.cathode
  N2: Part1.5V, R1.Pin_1, R2.Pin_1, R3.Pin_1, R4.Pin_1
  N3: S1.leg0, R1.Pin_0
  N4: S1.leg1, LED4.anode
  N5: S2.leg0, R3.Pin_0
  N6: S2.leg1, LED2.anode
  N7: S3.leg0, R4.Pin_0
  N8: S3.leg1, LED1.anode
  N9: S4.leg0, R2.Pin_0
  N10: S4.leg1, LED3.anode
