# Fritzing sketch Improved_Touch_Lamp (saved by Fritzing 0.8.0b)
breadboards: 1

parts:
  Part1 = Arduino Uno (Rev3)
  LED1 = LED - 5mm [color="White (4500K)" package="5 mm [THT]"]
  R1 = Resistor [tolerance=±5% resistance=220 package=THT]
  R2 = Resistor [tolerance=±5% resistance=1M package=THT]

nets:
  N1: Part1.ICSP_MISO, Part1.D12/MISO, LED1.anode
  N2: Part1.D2, R2.Pin_0
  N3: Part1.D4, R2.Pin_1
  N4: LED1.cathode, R1.Pin_0
