# Fritzing sketch Lights_Remote (saved by Fritzing 0.8.0b)
breadboards: 1

parts:
  Part1 = Arduino Uno (Rev3)
  U1 = Packages: [package=tssop28-groundpad]  # not connected
  LCD1 = LCD screen
  R1 = Resistor [tolerance=±5% resistance=220 package=THT]
  D1 = Rectifier Diode [part_number=1N4001 package="300 mil [THT]"]
  LED1 = LED - 5mm [color="Infrared (850nm)" package="5 mm [THT]"]
  R2 = Resistor [tolerance=±5% resistance=100 package=THT]
  S1 = Pushbutton [package=THT]
  S2 = Pushbutton [package=THT]
  S3 = Pushbutton [package=THT]
  S4 = Pushbutton [package=THT]
  R3 = Resistor [tolerance=±5% resistance=10k package=THT]
  R4 = Resistor [tolerance=±5% resistance=10k package=THT]
  R5 = Resistor [tolerance=±5% resistance=10k package=THT]
  R6 = Resistor [tolerance=±5% resistance=10k package=THT]

nets:
  GND: Part1.GND, LCD1.VSS, LCD1.V0, LCD1.R/W, R2.Pin_1, R3.Pin_0, R4.Pin_0, R5.Pin_0, R6.Pin_0
  N1: Part1.D8, S3.leg1, R5.Pin_1
  N2: Part1.D9_PWM, S2.leg1, R6.Pin_1
  N3: Part1.D10_PWM/SS, LCD1.DB6
  N4: Part1.D11_PWM/MOSI, LCD1.E
  N5: Part1.D12/MISO, LCD1.RS
  N6: Part1.D2, LCD1.DB7
  N7: Part1.D3_PWM, LED1.anode
  N8: Part1.D4, LCD1.DB5
  N9: Part1.D5_PWM, LCD1.DB4
  N10: Part1.D6_PWM, S4.leg1, R4.Pin_1
  N11: Part1.D7, S1.leg1, R3.Pin_1
  5V: Part1.5V, LCD1.VDD, R1.Pin_1, S1.leg0, S2.leg0, S3.leg0, S4.leg0
  N12: LCD1.LED+, D1.cathode
  N13: R1.Pin_0, D1.anode
  N14: LED1.cathode, R2.Pin_0
