# Fritzing sketch Potentionometer_Instrument (saved by Fritzing 0.8.0b)
breadboards: 1

parts:
  Part1 = Arduino Uno (Rev3)
  R1 = Rotary Potentiometer (Small)
  J1 = Piezo Speaker
  S1 = Pushbutton [package="[THT]"]
  R2 = Resistor [tolerance=±5% resistance=10k package=THT]

nets:
  N1: Part1.A0, R1.wiper
  N2: Part1.GND, R1.leg2, J1.pin1, R2.Pin_1
  N3: Part1.D8, J1.pin2
  N4: Part1.D2, S1.Pin_3, S1.Pin_4, R2.Pin_0
  N5: Part1.5V, R1.leg1, S1.Pin_1, S1.Pin_2
