# Fritzing sketch Simon_Says (saved by Fritzing 0.8.0b)
breadboards: 1

parts:
  Part1 = Arduino Uno (Rev3)
  S1 = Pushbutton [package=THT]
  S2 = Pushbutton [package=THT]
  S3 = Pushbutton [package=THT]
  S4 = Pushbutton [package=THT]
  LED1 = RGB LED (com. anode, rbg) [package="5 mm [THT]"]
  J1 = Piezo Speaker
  R1 = Resistor [tolerance=±5% resistance=220 package=THT]
  R2 = Resistor [tolerance=±5% resistance=220 package=THT]
  R3 = Resistor [tolerance=±5% resistance=220 package=THT]
  R4 = Resistor [tolerance=±5% resistance=220 package=THT]
  R5 = Resistor [tolerance=±5% resistance=220 package=THT]
  R6 = Resistor [tolerance=±5% resistance=220 package=THT]
  R7 = Resistor [tolerance=±5% resistance=220 package=THT]
  LED2 = LED - 5mm [color="Red (633nm)" package="5 mm [THT]"]
  LED3 = LED - 5mm [color="Blue (505nm)" package="5 mm [THT]"]
  LED4 = LED - 5mm [color="Yellow (595nm)" package="5 mm [THT]"]
  LED5 = LED - 5mm [color="Green (555nm)" package="5 mm [THT]"]
  R8 = Resistor [tolerance=±5% resistance=10k package=THT]
  R9 = Resistor [tolerance=±5% resistance=10k package=THT]
  R10 = Resistor [tolerance=±5% resistance=10k package=THT]
  R11 = Resistor [tolerance=±5% resistance=10k package=THT]

nets:
  N1: Part1.ICSP_MISO, Part1.D12/MISO, LED5.anode
  N2: Part1.ICSP_MOSI, Part1.D11_PWM/MOSI, R7.Pin_0
  N3: Part1.GND, LED1.blue_cathode, J1.pin1, R2.Pin_0, R3.Pin_0, R4.Pin_0, R5.Pin_0, R8.Pin_0, R9.Pin_0, R11.Pin_0
  N4: Part1.D8, S4.leg0, R8.Pin_1
  N5: Part1.D9_PWM, R1.Pin_0
  N6: Part1.D10_PWM/SS, R6.Pin_0
  N7: Part1.D13/SCK, J1.pin2
  N8: Part1.D2, S1.leg0, R11.Pin_1
  N9: Part1.D3_PWM, LED2.anode
  N10: Part1.D4, S2.leg0, R9.Pin_1
  N11: Part1.D5_PWM, LED3.anode
  N12: Part1.D6_PWM, S3.leg0, R10.Pin_1
  N13: Part1.D7, LED4.anode
  N14: Part1.5V, S1.leg1, S2.leg1, S3.leg1, S4.leg1
  N15: LED1.red_cathode, R7.Pin_1
  N16: LED1.common_anode, R6.Pin_1
  N17: LED1.green_cathode, R1.Pin_1
  N18: R2.Pin_1, LED2.cathode
  N19: R3.Pin_1, LED3.cathode
  N20: R4.Pin_1, LED4.cathode
  N21: R5.Pin_1, LED5.cathode
