# Fritzing sketch Temp_Lights (saved by Fritzing 0.8.0b)
breadboards: 1

parts:
  Part1 = Arduino Uno (Rev3)
  T1 = LM35 Temperature Sensor [package="TO92 [THT]"]
  LED1 = RGB LED (com. anode, rbg) [package="5 mm [THT]"]
  R1 = Resistor [tolerance=±5% resistance=220 package=THT]
  R2 = Resistor [tolerance=±5% resistance=220 package=THT]
  R3 = Resistor [tolerance=±5% resistance=220 package=THT]

nets:
  N1: Part1.A0, T1.Vout
  N2: Part1.ICSP_MOSI, Part1.D11_PWM/MOSI, R1.Pin_1
  GND: Part1.GND, T1.GND, LED1.common_anode
  N3: Part1.D9_PWM, R2.Pin_1
  N4: Part1.D10_PWM/SS, R3.Pin_1
  N5: Part1.5V, T1.+Vs
  N6: LED1.red_cathode, R1.Pin_0
  N7: LED1.blue_cathode, R3.Pin_0
  N8: LED1.green_cathode, R2.Pin_0
